# Fritzing sketch connection sketch (saved by Fritzing 0.9.2b)
breadboards: 1

parts:
  Part1 = Arduino Uno (Rev3)
  Part2 = Thumb Joystick
  J2 = Basic Servo
  J3 = Basic Servo

nets:
  N1: Part1.A0, Part2.HORZ
  N2: Part1.A1, Part2.VERT
  N3: Part1.A2, Part2.SEL
  N4: Part1.D9_PWM, J3.pulse
  N5: Part1.D10_PWM/SS, J2.pulse
  VCC: Part1.5V, Part2.VCC, J2.vcc, J3.vcc
  GND: Part1.GND, Part2.GND, J2.gnd, J3.gnd
